# Fritzing sketch circuit (saved by Fritzing 0.9.3b)
breadboards: 1

parts:
  RHT1 = Humidity and Temperature Sensor RHT03
  D1 = LTE-302 [package=lte-302]
  Q1 = NPN-Transistor [package="SOT-23 [SMD]"]
  WeMos_D1_Mini1 = WeMos D1 Mini

nets:
  VCC: RHT1.Vcc, D1.A, Q1.2, WeMos_D1_Mini1.5V
  N1: RHT1.Data-signal, WeMos_D1_Mini1.D2
  N2: RHT1.GND_1, WeMos_D1_Mini1.G
  N3: D1.C, Q1.1
  N4: Q1.0, WeMos_D1_Mini1.D1
